// Logisim project VRT64logisim.circ as structural Verilog
module HA (
  input  A,
  input  B,
  output CARRY,
  output SUM
);

  and and_1 (CARRY, A, B);
  xor xor_1 (SUM, A, B);
endmodule

module FA (
  input  A,
  input  B,
  input  CIN,
  output COUT,
  output SUM
);

  wire ha_1_carry, ha_1_sum, ha_2_carry;

  HA ha_1 (.A(A), .B(B), .CARRY(ha_1_carry), .SUM(ha_1_sum));
  HA ha_2 (.A(ha_1_sum), .B(CIN), .CARRY(ha_2_carry), .SUM(SUM));
  or or_1 (COUT, ha_1_carry, ha_2_carry);
endmodule

module FA4B (
  input  [3:0] A,
  input  [3:0] B,
  input  CIN,
  output [3:0] SUM,
  output COUT
);

  wire fa_1_cout, fa_2_cout, fa_3_cout;

  FA fa_1 (.A(A[0]), .B(B[0]), .CIN(CIN), .COUT(fa_1_cout), .SUM(SUM[0]));
  FA fa_2 (.A(A[1]), .B(B[1]), .CIN(fa_1_cout), .COUT(fa_2_cout), .SUM(SUM[1]));
  FA fa_3 (.A(A[2]), .B(B[2]), .CIN(fa_2_cout), .COUT(fa_3_cout), .SUM(SUM[2]));
  FA fa_4 (.A(A[3]), .B(B[3]), .CIN(fa_3_cout), .COUT(COUT), .SUM(SUM[3]));
endmodule

module ALU (
  input  [3:0] A,
  input  [3:0] B,
  input  SUB,
  input  ADD,
  output [3:0] SUM,
  output COUT
);

  wire or_1_out;
  wire [3:0] xor_1_out;
  wire [3:3] s_r_ff_1_q;

  or or_1 (or_1_out, SUB, ADD);
  S_R_Flip_Flop s_r_ff_1 (.S(SUB), .R(ADD), .clk(or_1_out), .Q(s_r_ff_1_q[3]));  // open: reset, Qn, preset
  assign xor_1_out = B ^ {4{s_r_ff_1_q[3]}};  // XOR_Gate xor_1, 4 bits wide
  FA4B fa4b_1 (.A(A), .B(xor_1_out), .CIN(s_r_ff_1_q[3]), .SUM(SUM), .COUT(COUT));
endmodule

module SR (
  input  S,
  input  R,
  output Q,
  output QNOT
);

  wire or_1_out;

  S_R_Flip_Flop s_r_ff_1 (.S(S), .R(R), .clk(or_1_out), .Q(Q), .Qn(QNOT));  // open: reset, preset
  or or_1 (or_1_out, S, R);
endmodule

module CPU (
  input  [3:0] B,
  input  CLOCK,
  output [3:0] out_3
);

  wire decoder_1_out12, decoder_1_out13, decoder_1_out14, decoder_1_out15;
  wire [3:0] alu_1_sum, Instructions_q, opcode_1_out_3, opcode_2_out_3, opcode_3_out_3, opcode_4_out_3,
       or_1_out;

  Register #(.width(4)) Instructions (.D(B), .en(decoder_1_out15), .clk(CLOCK), .Q(Instructions_q));  // open: clr
  OPCODE opcode_1 (.out_3(opcode_1_out_3));  // open: in_1, in_2
  OPCODE opcode_2 (.out_3(opcode_2_out_3));  // open: in_1, in_2
  OPCODE opcode_3 (.out_3(opcode_3_out_3));  // open: in_1, in_2
  OPCODE opcode_4 (.out_3(opcode_4_out_3));  // open: in_1, in_2
  assign or_1_out = opcode_1_out_3 | opcode_2_out_3 | opcode_3_out_3 | opcode_4_out_3;  // OR_Gate or_1, 4 bits wide
  Decoder #(.disabled("Z"), .enable("false"), .select(4)) decoder_1 (
    .out12(decoder_1_out12), .out13(decoder_1_out13), .out14(decoder_1_out14), .out15(decoder_1_out15),
    .sel(or_1_out));  // open: out0, out1, out2, out3, out4, out5, out6, out7, out8, out9, out10, out11
  ALU alu_1 (
    .A(out_3), .B(Instructions_q), .SUB(decoder_1_out13), .ADD(decoder_1_out14), .SUM(alu_1_sum));  // open: COUT
  Register #(.width(4)) Accumulator (.D(alu_1_sum), .en(decoder_1_out12), .clk(CLOCK), .Q(out_3));  // open: clr
endmodule

module CU (
  input  [2:0] INSTIN,
  output out_2,
  output out_3,
  output out_4,
  output out_5,
  output out_6,
  output out_7,
  output out_8,
  output out_9
);

  Decoder #(.enable("false"), .select(3), .tristate("true")) decoder_1 (
    .out0(out_2), .out1(out_3), .out2(out_4), .out3(out_5), .out4(out_6), .out5(out_7), .out6(out_8),
    .out7(out_9), .sel(INSTIN));
endmodule

module OPCODE (
  input  in_1,
  input  [1:0] in_2,
  output [3:0] out_3
);

  Decoder #(.disabled("Z"), .select(2), .tristate("true")) decoder_1 (
    .out0(out_3[0]), .out1(out_3[1]), .out2(out_3[2]), .out3(out_3[3]), .sel(in_2), .en(in_1));
endmodule

module PC (
);

  wire j_k_ff_1_q;

  J_K_Flip_Flop j_k_ff_1 (.Q(j_k_ff_1_q));  // open: J, K, clk, Qn, preset, reset
  J_K_Flip_Flop j_k_ff_2 (.J(j_k_ff_1_q));  // open: K, clk, Q, Qn, preset, reset
endmodule
